# Fritzing sketch cristo (saved by Fritzing 0.9.3b)

parts:
  Componente1 = Arduino Nano (Rev3.0)
  KY-1 = Keyes Relay [package=THT]
  VCC1 = Battery

nets:
  N1: Componente1.GND, KY-1.ground
  N2: Componente1.D7, KY-1.signal
  N3: Componente1.5V, KY-1.power
  N4: KY-1.NO, VCC1.+

notes:
  ElectroIman

custom parts:
  Keyes Relay: The Keyes 5V relay module is suitable for SCM development, home appliance control. It uses a 5V~12V TIL control signal which can control DC / AC signal.
